# Fritzing sketch SerialControlAnalogOutput (saved by Fritzing 0.9.3b)
breadboards: 1

parts:
  A1 = Arduino Uno (Rev3)
  C1 = Electrolytic Capacitor [capacitance=10µF package="100 mil [THT, electrolytic]"]
  R2 = Trimmer Potentiometer [maximum_resistance=5kΩ package=THT]
  U1 = LM358 [package=dip08]
  C1_2 = Electrolytic Capacitor [capacitance=10µF package="100 mil [THT, electrolytic]"]
  C1_3 = Electrolytic Capacitor [capacitance=10µF package="100 mil [THT, electrolytic]"]
  R2_2 = Trimmer Potentiometer [maximum_resistance=5kΩ package=THT]
  R2_3 = Trimmer Potentiometer [maximum_resistance=5kΩ package=THT]
  U1_2 = LM358 [package=dip08]
  U2 = BNC [package=bnc]
  R1 = Resistor [tolerance=±5% resistance=470 package=THT]
  R1_2 = Resistor [tolerance=±5% resistance=470 package=THT]
  R1_3 = Resistor [tolerance=±5% resistance=470 package=THT]
  R1_4 = Resistor [tolerance=±5% resistance=470 package=THT]
  R1_5 = Resistor [tolerance=±5% resistance=470 package=THT]
  R1_6 = Resistor [tolerance=±5% resistance=470 package=THT]
  U2_2 = BNC [package=bnc]
  U2_3 = BNC [package=bnc]
  U2_4 = BNC [package=bnc]
  U2_5 = BNC [package=bnc]
  U2_6 = BNC [package=bnc]
  U3 = LM 358 Dual Op-Amp [package="DIP8 [THT]"]

nets:
  GND: A1.GND, C1.-, U1.G$1_V-, C1_2.-, C1_3.-, U1_2.G$1_V-, U2.GND, R1_2.Pin_1, R1_3.Pin_0, R1_5.Pin_1, U2_2.GND, U2_3.GND, U2_4.GND, U2_5.GND, U2_6.GND
  N1: A1.D2, U1.G$1_+IN
  N2: A1.D3_PWM, R2.leg1
  N3: A1.D4, U2_5.OUT
  N4: A1.D5_PWM, R2_3.leg1
  N5: A1.D6_PWM, R2_2.leg1
  N6: A1.D7, U2_6.OUT
  N7: A1.VIN, U1.G$1_V+, U1_2.G$1_V+
  N8: C1.+, R2.wiper, U1_2.G$2_+IN
  N9: U1.G$1_OUT, U2.OUT, R1_5.Pin_0, R1_6.Pin_1
  N10: U1.G$1_-IN, R1_6.Pin_0
  N11: U1.G$2_+IN, C1_3.+, R2_2.wiper
  N12: U1.G$2_-IN, U1.G$2_OUT, U2_4.OUT
  N13: C1_2.+, R2_3.wiper, U1_2.G$1_+IN
  N14: U1_2.G$1_OUT, R1_3.Pin_1, R1_4.Pin_0, U2_3.OUT
  N15: U1_2.G$1_-IN, R1_4.Pin_1
  N16: U1_2.G$2_-IN, R1.Pin_0
  N17: U1_2.G$2_OUT, R1.Pin_1, R1_2.Pin_0, U2_2.OUT
  N18: U3.connector0, U3.connector7
  N19: U3.connector1, U3.connector6
  N20: U3.connector2, U3.connector5
  N21: U3.connector3, U3.connector4
